# Fritzing sketch etobi-shield (saved by Fritzing 0.9.3b)
circuit board: 6.46cm x 5.62921cm
breadboards: 2

parts:
  R1 = Resistor [tolerance=±5% resistance=47k package=THT]
  R2 = Resistor [tolerance=±5% resistance=47k package=THT]
  R3 = Resistor [tolerance=±5% resistance=47k package=THT]
  R6 = Resistor [tolerance=±5% resistance=330 package=THT]
  B3_(24) = Pushbutton [package="[THT]"]
  DS18b20 = LM35 Temperature Sensor [package="TO92 [THT]"]
  R8 = Resistor [tolerance=±5% resistance=4.7 package=THT]
  I2C = female pin header, 4 pins [form="♀ (female)"]
  1wire_(4) = screw terminal, 3 pins
  L3_(15) = LED - 3mm [color="Blue (525nm)" package="3 mm [THT]"]
  L2_(18) = LED - 3mm [color="Green (570nm)" package="3 mm [THT]"]
  L1_(14) = LED - 3mm [color="Red (633nm)" package="3 mm [THT]"]
  B4_(25) = Pushbutton [package="[THT]"]
  CH5 = female pin header, 2 pins [form="♀ (female)"]
  1wire = female pin header, 3 pins [form="♀ (female)"]
  CH1 = female pin header, 2 pins [form="♀ (female)"]
  CH0 = female pin header, 2 pins [form="♀ (female)"]
  R10 = Resistor [tolerance=±5% resistance=47k package=THT]
  CH2 = female pin header, 2 pins [form="♀ (female)"]
  CH3 = female pin header, 2 pins [form="♀ (female)"]
  CH4 = female pin header, 2 pins [form="♀ (female)"]
  B1_(23) = Pushbutton [package="[THT]"]
  B2_(22) = Pushbutton [package="[THT]"]
  R13 = Resistor [tolerance=±5% resistance=330 package=THT]
  L4_(27) = LED - 3mm [color="Blue (525nm)" package="3 mm [THT]"]
  R14 = Resistor [tolerance=±5% resistance=330 package=THT]
  R5 = Resistor [tolerance=±5% resistance=330 package=THT]
  R15 = Resistor [tolerance=±5% resistance=47k package=THT]
  R16 = Resistor [tolerance=±5% resistance=47k package=THT]
  Raspberry_Pi_1 = Raspberry Pi 3 [part_number=RPI-3-V1.2]
  I2C_2 = female pin header, 4 pins [form="♀ (female)"]
  R17 = Resistor [tolerance=±5% resistance=47k package=THT]
  R18 = Resistor [tolerance=±5% resistance=47k package=THT]
  MCP3208 = IC, DIP package, 16 pins [chip_label=MCP3208]

nets:
  GND: R1.Pin_0, R2.Pin_0, R3.Pin_0, R6.Pin_1, B3_(24).Pin_1, B3_(24).Pin_2, DS18b20.GND, I2C.pin1, 1wire_(4).pin3, B4_(25).Pin_1, B4_(25).Pin_2, 1wire.pin3, R10.Pin_0, B1_(23).Pin_1, B1_(23).Pin_2, B2_(22).Pin_1, B2_(22).Pin_2, R13.Pin_1, R14.Pin_1, R5.Pin_1, R15.Pin_0, R16.Pin_0, Raspberry_Pi_1.GND, I2C_2.pin1, R17.Pin_0, R18.Pin_0, MCP3208.pin9, MCP3208.pin14
  N1: R1.Pin_1, CH0.pin2, MCP3208.pin1
  N2: R2.Pin_1, CH1.pin2, MCP3208.pin2
  N3: R3.Pin_1, CH2.pin2, MCP3208.pin3
  N4: R6.Pin_0, L4_(27).cathode
  N5: B3_(24).Pin_3, B3_(24).Pin_4, Raspberry_Pi_1.GPIO24
  3V3: DS18b20.+Vs, R8.Pin_1, I2C.pin2, 1wire_(4).pin1, CH5.pin1, 1wire.pin1, CH1.pin1, CH0.pin1, CH2.pin1, CH3.pin1, CH4.pin1, Raspberry_Pi_1.3v3, Raspberry_Pi_1.3V3, I2C_2.pin2, MCP3208.pin15, MCP3208.pin16
  N6: DS18b20.Vout, R8.Pin_0, 1wire_(4).pin2, 1wire.pin2, Raspberry_Pi_1.GPIO4
  N7: I2C.pin3, Raspberry_Pi_1.GPIO2, I2C_2.pin4
  N8: I2C.pin4, Raspberry_Pi_1.GPIO3, I2C_2.pin3
  N9: L3_(15).cathode, R13.Pin_0
  N10: L3_(15).anode, Raspberry_Pi_1.GPIO15
  N11: L2_(18).cathode, R14.Pin_0
  N12: L2_(18).anode, Raspberry_Pi_1.GPIO18
  N13: L1_(14).cathode, R5.Pin_0
  N14: L1_(14).anode, Raspberry_Pi_1.GPIO14
  N15: B4_(25).Pin_3, B4_(25).Pin_4, Raspberry_Pi_1.GPIO25
  N16: CH5.pin2, R10.Pin_1, MCP3208.pin6
  N17: CH3.pin2, R15.Pin_1, MCP3208.pin4
  N18: CH4.pin2, R16.Pin_1, MCP3208.pin5
  N19: B1_(23).Pin_3, B1_(23).Pin_4, Raspberry_Pi_1.GPIO23
  N20: B2_(22).Pin_3, B2_(22).Pin_4, Raspberry_Pi_1.GPIO22
  N21: L4_(27).anode, Raspberry_Pi_1.GPIO27
  N22: Raspberry_Pi_1.GPIO10, MCP3208.pin11
  N23: Raspberry_Pi_1.GPIO9, MCP3208.pin12
  N24: Raspberry_Pi_1.GPIO11, MCP3208.pin13
  N25: Raspberry_Pi_1.GPIO8, MCP3208.pin10
  N26: R17.Pin_1, MCP3208.pin7
  N27: R18.Pin_1, MCP3208.pin8

notes:
  SDA
  SDL
  3.3V
  GND
  DATA
  etobi.de
  v1.0.2 2016-08-13
